// Logisim project ALU.circ as structural Verilog: 1 circuit, main circuit main
module main (
  input  [15:0] inputA,
  input  [15:0] inputB,
  input  [7:0] ALUControl,
  output [15:0] result,
  output Flag
);

  wire [15:0] main_1_output, main_2_sum_diff, main_3_output;

  ShiftBlock_main main_1 (
    .Register(inputA), .ShiftOperation(ALUControl[5:4]), .ShiftAmount(inputB[3:0]), .Output(main_1_output));
  ArithmaticBlock_main main_2 (
    .inputA(inputA), .inputB(inputB), .sum_diff(main_2_sum_diff),
    .ArethmeticOp__0__add___1__sub___2__slt___3_sltu(ALUControl[3:2]), .Zero(Flag));
  LogicBlock_main main_3 (.inputA(inputA), .inputB(inputB), .\output (main_3_output), .logicOperation(ALUControl[7:6]));
  Multiplexer #(.select(2), .width(16)) multiplexer_1 (
    .in0(main_1_output), .in1(main_2_sum_diff), .in2(main_3_output), .out(result), .sel(ALUControl[1:0]),
    .en(1'b1));  // open: in3

  // Notes on the sheet:
  //   ALUControl(8) = LogicOP(2)+ShiftOp(2)+ArithmeticOp(2)+ALUOP(2) 
endmodule
