// Logisim project ArithmaticBlock.circ as structural Verilog: 1 circuit, main circuit main
module main (
  input  [15:0] inputA,
  input  [15:0] inputB,
  input  [1:0] ArethmeticOp__0__add___1__sub___2__slt___3_sltu,
  output [15:0] sum_diff,
  output Zero
);

  wire comparator_2_lt, comparator_3_lt;
  wire [15:0] adder_1_out, bit_extender_1_out, bit_extender_2_out, subtractor_1_out;

  Adder #(.width(16)) adder_1 (.a(inputA), .b(inputB), .out(adder_1_out), .cin(1'b0));  // open: cout
  Subtractor #(.width(16)) subtractor_1 (.a(inputA), .b(inputB), .out(subtractor_1_out), .bin(1'b0));  // open: bout
  Comparator #(.width(16)) comparator_1 (.a(inputB), .b({16{1'b0}}), .eq(Zero));  // open: gt, lt
  Comparator #(.width(16), .mode("unsigned")) comparator_2 (
    .a(inputA), .b(inputB), .lt(comparator_2_lt));  // open: gt, eq
  Comparator #(.width(16)) comparator_3 (.a(inputA), .b(inputB), .lt(comparator_3_lt));  // open: gt, eq
  assign bit_extender_1_out = {{15{1'b0}}, comparator_2_lt};  // Bit_Extender bit_extender_1
  assign bit_extender_2_out = {{15{1'b0}}, comparator_3_lt};  // Bit_Extender bit_extender_2
  Multiplexer #(.select(2), .width(16), .enable("false")) multiplexer_1 (
    .in0(adder_1_out), .in1(subtractor_1_out), .in2(bit_extender_2_out), .in3(bit_extender_1_out),
    .out(sum_diff), .sel(ArethmeticOp__0__add___1__sub___2__slt___3_sltu));

  // Notes on the sheet:
  //   unsigned
  //   signed
endmodule
