// Logisim project ControlUnit.circ as structural Verilog: 1 circuit, main circuit main
module main (
  input  [4:0] opCode,
  input  [1:0] func,
  output RegDst,
  output RegWrite,
  output signExt,
  output ALUsrc,
  output jal,
  output [5:0] NextPcControl,
  output MemRead,
  output MemWrite,
  output [1:0] MemToReg,
  output setOp,
  output [7:0] ALUOp
);

  wire and_1_out, and_2_out, and_5_out, and_6_out, and_7_out, and_8_out, and_9_out, and_10_out, and_11_out,
       and_12_out, and_13_out, decoder_1_out0, decoder_1_out1, decoder_1_out3, decoder_1_out4,
       decoder_1_out5, decoder_1_out6, decoder_1_out7, decoder_1_out8, decoder_1_out9, decoder_1_out10,
       decoder_1_out11, decoder_1_out12, decoder_1_out13, decoder_1_out28, decoder_2_out0, decoder_2_out1,
       decoder_2_out2, decoder_2_out3;

  Decoder #(.select(5), .enable("false")) decoder_1 (
    .out0(decoder_1_out0), .out1(decoder_1_out1), .out3(decoder_1_out3), .out4(decoder_1_out4),
    .out5(decoder_1_out5), .out6(decoder_1_out6), .out7(decoder_1_out7), .out8(decoder_1_out8),
    .out9(decoder_1_out9), .out10(decoder_1_out10), .out11(decoder_1_out11), .out12(decoder_1_out12),
    .out13(decoder_1_out13), .out16(MemRead), .out17(MemWrite), .out24(NextPcControl[1]),
    .out25(NextPcControl[0]), .out28(decoder_1_out28), .out29(setOp), .out30(NextPcControl[4]), .out31(jal),
    .sel(opCode));  // open: out2, out14, out15, out18, out19, out20, out21, out22, out23, out26, out27
  Decoder #(.select(2), .enable("false")) decoder_2 (
    .out0(decoder_2_out0), .out1(decoder_2_out1), .out2(decoder_2_out2), .out3(decoder_2_out3), .sel(func));
  and and_1 (and_1_out, decoder_1_out3, decoder_2_out1);
  or or_1 (RegDst, decoder_1_out0, decoder_1_out1, and_1_out);
  and and_2 (and_2_out, decoder_1_out3, decoder_2_out0);
  nor nor_1 (RegWrite, and_2_out, MemWrite, NextPcControl[1], NextPcControl[0], NextPcControl[4]);
  or or_2 (signExt, decoder_1_out4, decoder_1_out5, decoder_1_out6, decoder_1_out7, MemRead, MemWrite, decoder_1_out12);
  nor nor_2 (ALUsrc, decoder_1_out1, decoder_1_out0, NextPcControl[1], NextPcControl[0]);
  and and_3 (NextPcControl[3], decoder_1_out3, decoder_2_out1);
  and and_4 (NextPcControl[5], decoder_2_out0, decoder_1_out3);
  and and_5 (and_5_out, decoder_2_out1, decoder_1_out3);
  or or_3 (MemToReg[1], jal, decoder_1_out28, setOp, and_5_out);
  or or_4 (MemToReg[0], and_5_out, jal, MemRead);
  and and_6 (and_6_out, decoder_1_out1, decoder_2_out2);
  or or_5 (ALUOp[7], decoder_1_out6, decoder_1_out7, and_6_out, and_7_out);
  and and_7 (and_7_out, decoder_1_out1, decoder_2_out3);
  and and_8 (and_8_out, decoder_1_out1, decoder_2_out1);
  and and_9 (and_9_out, decoder_1_out1, decoder_2_out3);
  or or_6 (ALUOp[6], decoder_1_out7, and_8_out, and_9_out);
  or or_7 (ALUOp[4], decoder_1_out9, decoder_1_out11);
  or or_8 (ALUOp[5], decoder_1_out10, decoder_1_out11);
  and and_10 (and_10_out, decoder_1_out0, decoder_2_out2);
  or or_9 (ALUOp[3], and_10_out, and_11_out, decoder_1_out12, decoder_1_out13);
  and and_11 (and_11_out, decoder_1_out0, decoder_2_out3);
  and and_12 (and_12_out, decoder_2_out1, decoder_1_out0);
  and and_13 (and_13_out, decoder_2_out3, decoder_1_out0);
  or or_10 (ALUOp[2], and_12_out, and_13_out, decoder_1_out13);
  or or_11 (ALUOp[1], decoder_1_out1, decoder_1_out6, decoder_1_out7, decoder_1_out5);
  or or_12 (ALUOp[0], decoder_1_out0, decoder_1_out4, decoder_1_out12, decoder_1_out13, MemRead, MemWrite);

  assign NextPcControl[2] = jal;

  // Notes on the sheet:
  //   R0
  //   R1
  //   R3
  //   addi
  //   andi
  //   ori
  //   xori
  //   sll
  //   srl
  //   sra
  //   ror
  //   slti
  //   sltiu
  //   lw
  //   sw
  //   bez
  //   bnz
  //   set
  //   seth
  //   j
  //   jal
endmodule
