// Logisim project Ext.circ as structural Verilog: 1 circuit, main circuit main
module main (
  input  [4:0] Imm_5,
  input  ExtSrc,
  output [15:0] Output
);

  wire [15:0] bit_extender_1_out, bit_extender_2_out;

  assign bit_extender_1_out = {{11{1'b0}}, Imm_5};  // Bit_Extender bit_extender_1
  assign bit_extender_2_out = {{11{Imm_5[4]}}, Imm_5};  // Bit_Extender bit_extender_2
  Multiplexer #(.width(16), .enable("false")) multiplexer_1 (
    .in0(bit_extender_1_out), .in1(bit_extender_2_out), .out(Output), .sel(ExtSrc));
endmodule
