// Logisim project LogicBlock.circ as structural Verilog: 1 circuit, main circuit main
module main (
  input  [15:0] inputA,
  input  [15:0] inputB,
  input  [1:0] logicOperation,
  output [15:0] \output 
);

  wire [15:0] and_1_out, and_2_out, or_1_out, xor_1_out;

  assign xor_1_out = inputA ^ inputB;  // XOR_Gate xor_1, 16 bits wide
  assign or_1_out = inputA | inputB;  // OR_Gate or_1, 16 bits wide
  assign and_1_out = inputA & inputB;  // AND_Gate and_1, 16 bits wide
  assign and_2_out = inputA & ~inputB;  // AND_Gate and_2, 16 bits wide
  Multiplexer #(.select(2), .width(16)) multiplexer_1 (
    .in0(and_1_out), .in1(and_2_out), .in2(or_1_out), .in3(xor_1_out), .out(\output ), .sel(logicOperation),
    .en(1'b1));
endmodule
