// Logisim project Pipelined Processor.circ as structural Verilog: 11 circuits, main circuit main
module main (
  input  in_1,
  input  in_2,
  input  in_3,
  input  reset
);

  wire ALUSrc, ALUSrcP, clock_1_out, controlpipeline_1_out_15, EarlyNextPcSrc, jal, main_5_flag, MemRead1,
       MemReadP, MemRed, MemWrite, MemWriteP, or_1_out, or_2_out, PcSrc, RegDst, RegWrite, RegWrite1,
       RegWrite2, RegWriteP, setOp, setOpP, SignExt, SignExtP, Stall, stallmux_1_out_11, stallmux_1_out_12,
       stallmux_1_out_13, stallmux_1_out_14, stallmux_1_out_15, stallmux_1_out_17;
  wire [1:0] ForwardA, ForwardB, func, MemToReg, MemToReg1, MemToRegP, stallmux_1_out_16;
  wire [2:0] main_2_rd, multiplexer_4_out, multiplexer_5_out, Rd1, Rd2, Rd3, Rs, Rt;
  wire [4:0] Imm5, OP, registerpipeline_1_out_11;
  wire [5:0] NextPcControl, NextPcControlP, stallmux_1_out_18;
  wire [7:0] ALUOp, ALUOpP, Imm8, imm8_t, stallmux_1_out_19;
  wire [10:0] main_2_imm_11, registerpipeline_1_out_10;
  wire [15:0] adder_1_out, adder_2_out, adder_3_out, alupipeline_1_out_7, alupipeline_1_out_8,
       alupipeline_1_out_9, alupipeline_1_out_10, ALURestult, BusW, EarlyNextPc, main_3_busa, main_3_busb,
       main_4_output, multiplexer_1_out, multiplexer_2_out, multiplexer_3_out, multiplexer_6_out,
       multiplexer_7_out, multiplexer_8_out, multiplexer_9_out, MuxRestult, nextPC, PC_q, pipeline_1_out_5,
       pipeline_1_out_6, ram_1_data, registerpipeline_1_out_9, registerpipeline_1_out_13,
       registerpipeline_1_out_14, rom_1_data, SETResult;

  Multiplexer #(.width(16), .enable("false")) multiplexer_1 (
    .in0(adder_2_out), .in1(nextPC), .out(multiplexer_1_out), .sel(PcSrc));
  ControlUnit_main main_1 (
    .opCode(OP), .func(func), .RegDst(RegDst), .RegWrite(RegWriteP), .signExt(SignExtP), .ALUsrc(ALUSrcP),
    .MemRead(MemReadP), .MemWrite(MemWriteP), .setOp(setOpP), .MemToReg(MemToRegP), .ALUOp(ALUOpP),
    .NextPcControl(NextPcControlP), .jal(jal));
  Multiplexer #(.width(16), .enable("false")) multiplexer_2 (
    .in0(multiplexer_1_out), .in1(EarlyNextPc), .out(multiplexer_2_out), .sel(EarlyNextPcSrc));
  Register #(.width(16)) PC (.D(multiplexer_2_out), .en(in_1), .Q(PC_q), .clk(clock_1_out), .clr(reset));
  Adder #(.width(16)) adder_1 (.a(PC_q), .b({16{1'b1}}), .out(adder_1_out));  // open: cin, cout
  Multiplexer #(.width(16), .enable("false")) multiplexer_3 (
    .in0(PC_q), .in1(adder_1_out), .out(multiplexer_3_out), .sel(Stall));
  Adder #(.width(16)) adder_2 (.a(16'h1), .b(multiplexer_3_out), .out(adder_2_out));  // open: cin, cout
  ROM #(.addrWidth(16), .dataWidth(16)) rom_1 (.addr(multiplexer_3_out), .data(rom_1_data), .sel(in_2));
  or or_1 (or_1_out, EarlyNextPcSrc, PcSrc);
  pipeLine pipeline_1 (
    .in_1(multiplexer_3_out), .in_2(rom_1_data), .in_4(clock_1_out), .out_5(pipeline_1_out_5),
    .out_6(pipeline_1_out_6), .in_3(or_1_out));
  Splitter_main main_2 (
    .Rt(Rt), .Rs(Rs), .Rd(main_2_rd), .f(func), .Op(OP), .Imm_5(Imm5), .Imm_8(Imm8), .Imm_11(main_2_imm_11),
    .in_1(pipeline_1_out_6));
  Multiplexer #(.width(3), .enable("false")) multiplexer_4 (
    .in0(Rt), .in1(main_2_rd), .out(multiplexer_4_out), .sel(RegDst));
  Multiplexer #(.width(3), .enable("false")) multiplexer_5 (
    .in0(multiplexer_4_out), .in1(3'b111), .out(multiplexer_5_out), .sel(jal));
  Clock clock_1 (.out(clock_1_out));
  RegFile_main main_3 (
    .RA(Rs), .RB(Rt), .RW(Rd3), .BusW(BusW), .RegWrite(RegWrite), .BusA(main_3_busa), .BusB(main_3_busb),
    .in_5(clock_1_out), .in_6(reset));
  Multiplexer #(.select(2), .width(16), .enable("false")) multiplexer_6 (
    .in0(ALURestult), .in2(SETResult), .out(multiplexer_6_out), .sel(MemToReg1));  // open: in1, in3
  // Probe on BusW
  ForwardngUnit forwardngunit_1 (
    .RegWrite1(RegWrite1), .Rd1(Rd1), .RegWrite2(RegWrite2), .Rd2(Rd2), .RegWrite3(RegWrite), .Rd3(Rd3),
    .Rs(Rs), .Rt(Rt), .ForwardA(ForwardA), .MemRead(MemRead1), .StallSignal(Stall), .ForwardB(ForwardB));
  Multiplexer #(.select(2), .width(16), .enable("false")) multiplexer_7 (
    .in0(main_3_busa), .in1(multiplexer_6_out), .in2(MuxRestult), .in3(BusW), .out(multiplexer_7_out),
    .sel(ForwardA));
  Multiplexer #(.select(2), .width(16), .enable("false")) multiplexer_8 (
    .in0(main_3_busb), .in1(multiplexer_6_out), .in2(MuxRestult), .in3(BusW), .out(multiplexer_8_out),
    .sel(ForwardB));
  EarlyJumpDetection earlyjumpdetection_1 (
    .PC(pipeline_1_out_5), .Imm11(main_2_imm_11), .Rs(multiplexer_7_out), .j_b_control(NextPcControlP),
    .nextPC(EarlyNextPc), .nextPCsrc(EarlyNextPcSrc));
  or or_2 (or_2_out, Stall, PcSrc);
  StallMux stallmux_1 (
    .in_1(RegWriteP), .in_2(SignExtP), .in_3(ALUSrcP), .in_4(MemReadP), .in_5(MemWriteP), .in_6(MemToRegP),
    .in_7(setOpP), .in_8(NextPcControlP), .in_9(ALUOpP), .out_11(stallmux_1_out_11),
    .out_12(stallmux_1_out_12), .out_13(stallmux_1_out_13), .out_14(stallmux_1_out_14),
    .out_15(stallmux_1_out_15), .out_16(stallmux_1_out_16), .out_17(stallmux_1_out_17),
    .out_18(stallmux_1_out_18), .out_19(stallmux_1_out_19), .in_10(or_2_out));
  registerPipeline registerpipeline_1 (
    .in_1(pipeline_1_out_5), .in_2(main_2_imm_11), .in_4(Imm8), .in_5(multiplexer_7_out),
    .in_6(multiplexer_8_out), .in_8(clock_1_out), .out_9(registerpipeline_1_out_9),
    .out_10(registerpipeline_1_out_10), .out_12(imm8_t), .out_13(registerpipeline_1_out_13),
    .out_14(registerpipeline_1_out_14), .in_3(Imm5), .out_11(registerpipeline_1_out_11),
    .in_7(multiplexer_5_out), .out_15(Rd1));
  controlPipeline controlpipeline_1 (
    .RegWrite(stallmux_1_out_11), .SignExt(stallmux_1_out_12), .ALUSrc(stallmux_1_out_13),
    .MemRead(stallmux_1_out_14), .MemWrite(stallmux_1_out_15), .MemToReg(stallmux_1_out_16),
    .setOp(stallmux_1_out_17), .NextPcControl(stallmux_1_out_18), .ALUOp(stallmux_1_out_19),
    .out_11(RegWrite1), .out_12(SignExt), .out_13(ALUSrc), .out_14(MemRead1),
    .out_15(controlpipeline_1_out_15), .out_16(MemToReg1), .out_17(setOp), .out_18(NextPcControl),
    .out_19(ALUOp), .in_10(clock_1_out));
  // Probe on nextPC
  Ext_main main_4 (.Imm_5(registerpipeline_1_out_11), .Output(main_4_output), .ExtSrc(SignExt));
  ALU_main main_5 (
    .inputA(registerpipeline_1_out_13), .inputB(multiplexer_9_out), .ALUControl(ALUOp), .result(ALURestult),
    .Flag(main_5_flag));
  Multiplexer #(.width(16), .enable("false")) multiplexer_9 (
    .in0(registerpipeline_1_out_14), .in1(main_4_output), .out(multiplexer_9_out), .sel(ALUSrc));
  nextPC_main main_6 (
    .PC(registerpipeline_1_out_9), .Imm11(registerpipeline_1_out_10), .flag(main_5_flag),
    .j_b_control(NextPcControl), .nextPC(nextPC), .nextPCsrc(PcSrc));
  set_main main_7 (.Imm_8(imm8_t), .BusB(registerpipeline_1_out_14), .out_4(SETResult), ._0__set___1__SetH(setOp));
  Adder #(.width(16)) adder_3 (.a(16'h1), .b(registerpipeline_1_out_9), .out(adder_3_out));  // open: cin, cout
  ALUPipeline alupipeline_1 (
    .in_1(ALURestult), .in_2(registerpipeline_1_out_14), .in_3(SETResult), .in_5(Rd1), .in_6(clock_1_out),
    .out_7(alupipeline_1_out_7), .out_8(alupipeline_1_out_8), .out_9(alupipeline_1_out_9), .out_11(Rd2),
    .in_4(adder_3_out), .out_10(alupipeline_1_out_10));
  controlALUPipeline controlalupipeline_1 (
    .regWrite(RegWrite1), .MemRead(MemRead1), .MemWrite(controlpipeline_1_out_15), .MemToReg(MemToReg1),
    .out_6(RegWrite2), .out_7(MemRed), .out_8(MemWrite), .out_9(MemToReg), .in_5(clock_1_out));
  RAM #(.addrWidth(16), .dataWidth(16), .bus("separate")) ram_1 (
    .addr(alupipeline_1_out_7), .din(alupipeline_1_out_8), .data(ram_1_data), .str(MemWrite), .sel(1'b1),
    .clk(clock_1_out), .ld(MemRed), .clr(in_3));
  Multiplexer #(.select(2), .width(16), .enable("false")) multiplexer_10 (
    .in0(alupipeline_1_out_7), .in1(ram_1_data), .in2(alupipeline_1_out_9), .in3(alupipeline_1_out_10),
    .out(MuxRestult), .sel(MemToReg));
  WBPipeline wbpipeline_1 (.in_1(MuxRestult), .in_2(Rd2), .in_3(clock_1_out), .out_4(BusW), .out_5(Rd3));
  controlWBPipeline controlwbpipeline_1 (.in_1(RegWrite2), .in_2(clock_1_out), .out_3(RegWrite));

  // Other names for the same wires on the sheet: RegWrite3 = RegWrite; Rw[2:0] = Rd3

  // Notes on the sheet:
  //   contents of rom_1 (hex, n*v repeats v):
  //   e049 8801 e029 8841 e7a1 8881 e7e1 88c1 e069 8901 e039 8941 e059 8981 e071 89c1 e019 8a01 e031 8a41
  //   e009 8a81 e079 8ac1 e011 8b01 e041 8b41 e051 8b81 e079 e002 e00b 27dc 8024 801d 5a5 c82e 27de 8835
  //   881c e00a 205b 599 cfae cf92
endmodule

module pipeLine (
  input  [15:0] in_1,
  input  [15:0] in_2,
  input  in_3,
  input  in_4,
  output [15:0] out_5,
  output [15:0] out_6
);

  wire [31:0] multiplexer_1_out;

  Multiplexer #(.width(32), .enable("false")) multiplexer_1 (
    .in0({in_2, in_1}), .in1({32{1'b0}}), .out(multiplexer_1_out), .sel(in_3));
  Register #(.width(32)) register_1 (.D(multiplexer_1_out), .Q({out_6, out_5}), .clk(in_4));  // open: en, clr
endmodule

module registerPipeline (
  input  [15:0] in_1,
  input  [10:0] in_2,
  input  [4:0] in_3,
  input  [7:0] in_4,
  input  [15:0] in_5,
  input  [15:0] in_6,
  input  [2:0] in_7,
  input  in_8,
  output [15:0] out_9,
  output [10:0] out_10,
  output [4:0] out_11,
  output [7:0] out_12,
  output [15:0] out_13,
  output [15:0] out_14,
  output [2:0] out_15
);

  Register #(.width(16)) PC (.D(in_1), .Q(out_9), .clk(in_8));  // open: en, clr
  Register #(.width(11)) imm11 (.D(in_2), .Q(out_10), .clk(in_8));  // open: en, clr
  Register #(.width(5)) imm5 (.D(in_3), .Q(out_11), .clk(in_8));  // open: en, clr
  Register imm8 (.D(in_4), .Q(out_12), .clk(in_8));  // open: en, clr
  Register #(.width(16)) BusA (.D(in_5), .Q(out_13), .clk(in_8));  // open: en, clr
  Register #(.width(16)) BusB (.D(in_6), .Q(out_14), .clk(in_8));  // open: en, clr
  Register #(.width(3)) register_1 (.D(in_7), .Q(out_15), .clk(in_8));  // open: en, clr
endmodule

module ALUPipeline (
  input  [15:0] in_1,
  input  [15:0] in_2,
  input  [15:0] in_3,
  input  [15:0] in_4,
  input  [2:0] in_5,
  input  in_6,
  output [15:0] out_7,
  output [15:0] out_8,
  output [15:0] out_9,
  output [15:0] out_10,
  output [2:0] out_11
);

  Register #(.width(16)) register_1 (.D(in_1), .Q(out_7), .clk(in_6));  // open: en, clr
  Register #(.width(16)) register_2 (.D(in_2), .Q(out_8), .clk(in_6));  // open: en, clr
  Register #(.width(16)) register_3 (.D(in_3), .Q(out_9), .clk(in_6));  // open: en, clr
  Register #(.width(16)) register_4 (.D(in_4), .Q(out_10), .clk(in_6));  // open: en, clr
  Register #(.width(3)) register_5 (.D(in_5), .Q(out_11), .clk(in_6));  // open: en, clr
endmodule

module WBPipeline (
  input  [15:0] in_1,
  input  [2:0] in_2,
  input  in_3,
  output [15:0] out_4,
  output [2:0] out_5
);

  Register #(.width(16)) register_1 (.D(in_1), .Q(out_4), .clk(in_3));  // open: en, clr
  Register #(.width(3)) register_2 (.D(in_2), .Q(out_5), .clk(in_3));  // open: en, clr
endmodule

module controlPipeline (
  input  RegWrite,
  input  SignExt,
  input  ALUSrc,
  input  MemRead,
  input  MemWrite,
  input  [1:0] MemToReg,
  input  setOp,
  input  [5:0] NextPcControl,
  input  [7:0] ALUOp,
  input  in_10,
  output out_11,
  output out_12,
  output out_13,
  output out_14,
  output out_15,
  output [1:0] out_16,
  output out_17,
  output [5:0] out_18,
  output [7:0] out_19
);

  Register #(.width(1)) register_1 (.D(RegWrite), .Q(out_11), .clk(in_10));  // open: en, clr
  Register #(.width(1)) register_2 (.D(SignExt), .Q(out_12), .clk(in_10));  // open: en, clr
  Register #(.width(1)) register_3 (.D(ALUSrc), .Q(out_13), .clk(in_10));  // open: en, clr
  Register #(.width(1)) register_4 (.D(MemRead), .Q(out_14), .clk(in_10));  // open: en, clr
  Register #(.width(1)) register_5 (.D(MemWrite), .Q(out_15), .clk(in_10));  // open: en, clr
  Register #(.width(2)) register_6 (.D(MemToReg), .Q(out_16), .clk(in_10));  // open: en, clr
  Register #(.width(1)) register_7 (.D(setOp), .Q(out_17), .clk(in_10));  // open: en, clr
  Register #(.width(6)) register_8 (.D(NextPcControl), .Q(out_18), .clk(in_10));  // open: en, clr
  Register register_9 (.D(ALUOp), .Q(out_19), .clk(in_10));  // open: en, clr
endmodule

module controlALUPipeline (
  input  regWrite,
  input  MemRead,
  input  MemWrite,
  input  [1:0] MemToReg,
  input  in_5,
  output out_6,
  output out_7,
  output out_8,
  output [1:0] out_9
);

  Register #(.width(1)) register_1 (.D(regWrite), .Q(out_6), .clk(in_5));  // open: en, clr
  Register #(.width(1)) register_2 (.D(MemRead), .Q(out_7), .clk(in_5));  // open: en, clr
  Register #(.width(1)) register_3 (.D(MemWrite), .Q(out_8), .clk(in_5));  // open: en, clr
  Register #(.width(2)) register_4 (.D(MemToReg), .Q(out_9), .clk(in_5));  // open: en, clr
endmodule

module ForwardngUnit (
  input  MemRead,
  input  RegWrite1,
  input  [2:0] Rd1,
  input  RegWrite2,
  input  [2:0] Rd2,
  input  RegWrite3,
  input  [2:0] Rd3,
  input  [2:0] Rs,
  input  [2:0] Rt,
  output StallSignal,
  output [1:0] ForwardB,
  output [1:0] ForwardA
);

  wire and_1_out, and_2_out, and_3_out, and_4_out, and_5_out, and_6_out, comparator_1_eq, comparator_2_eq,
       comparator_3_eq, comparator_4_eq, comparator_5_eq, comparator_6_eq, comparator_7_eq, comparator_8_eq,
       not_1_out, not_2_out, or_1_out;
  wire [1:0] multiplexer_1_out, multiplexer_2_out, multiplexer_3_out, multiplexer_5_out;

  Comparator #(.width(3), .mode("unsigned")) comparator_1 (.a(3'b000), .b(Rs), .eq(comparator_1_eq));  // open: gt, lt
  not not_1 (not_1_out, comparator_1_eq);
  Comparator #(.width(3), .mode("unsigned")) comparator_2 (.a(Rd1), .b(Rs), .eq(comparator_2_eq));  // open: gt, lt
  Comparator #(.width(3), .mode("unsigned")) comparator_3 (.a(Rd2), .b(Rs), .eq(comparator_3_eq));  // open: gt, lt
  Comparator #(.width(3), .mode("unsigned")) comparator_4 (.a(Rd3), .b(Rs), .eq(comparator_4_eq));  // open: gt, lt
  and and_1 (and_1_out, RegWrite1, not_1_out, comparator_2_eq);
  and and_2 (and_2_out, RegWrite2, not_1_out, comparator_3_eq);
  and and_3 (and_3_out, RegWrite3, not_1_out, comparator_4_eq);
  Comparator #(.width(3), .mode("unsigned")) comparator_5 (.a(3'b000), .b(Rt), .eq(comparator_5_eq));  // open: gt, lt
  not not_2 (not_2_out, comparator_5_eq);
  and and_4 (and_4_out, RegWrite1, not_2_out, comparator_6_eq);
  Comparator #(.width(3), .mode("unsigned")) comparator_6 (.a(Rd1), .b(Rt), .eq(comparator_6_eq));  // open: gt, lt
  and and_5 (and_5_out, RegWrite2, not_2_out, comparator_7_eq);
  Comparator #(.width(3), .mode("unsigned")) comparator_7 (.a(Rd2), .b(Rt), .eq(comparator_7_eq));  // open: gt, lt
  and and_6 (and_6_out, RegWrite3, not_2_out, comparator_8_eq);
  Comparator #(.width(3), .mode("unsigned")) comparator_8 (.a(Rd3), .b(Rt), .eq(comparator_8_eq));  // open: gt, lt
  or or_1 (or_1_out, and_1_out, and_4_out);
  Multiplexer #(.width(2), .enable("false")) multiplexer_1 (
    .in0(2'b00), .in1(2'b11), .out(multiplexer_1_out), .sel(and_6_out));
  and and_7 (StallSignal, MemRead, or_1_out);
  Multiplexer #(.width(2), .enable("false")) multiplexer_2 (
    .in0(multiplexer_1_out), .in1(2'b10), .out(multiplexer_2_out), .sel(and_5_out));
  Multiplexer #(.width(2), .enable("false")) multiplexer_3 (
    .in0(2'b00), .in1(2'b11), .out(multiplexer_3_out), .sel(and_3_out));
  Multiplexer #(.width(2), .enable("false")) multiplexer_4 (
    .in0(multiplexer_2_out), .in1(2'b01), .out(ForwardB), .sel(and_4_out));
  Multiplexer #(.width(2), .enable("false")) multiplexer_5 (
    .in0(multiplexer_3_out), .in1(2'b10), .out(multiplexer_5_out), .sel(and_2_out));
  Multiplexer #(.width(2), .enable("false")) multiplexer_6 (
    .in0(multiplexer_5_out), .in1(2'b01), .out(ForwardA), .sel(and_1_out));

  // Notes on the sheet:
  //   ForwardA = 1
  //   ForwardB = 1
endmodule

module controlWBPipeline (
  input  in_1,
  input  in_2,
  output out_3
);

  Register #(.width(1)) register_1 (.D(in_1), .Q(out_3), .clk(in_2));  // open: en, clr
endmodule

module StallMux (
  input  in_1,
  input  in_2,
  input  in_3,
  input  in_4,
  input  in_5,
  input  [1:0] in_6,
  input  in_7,
  input  [5:0] in_8,
  input  [7:0] in_9,
  input  in_10,
  output out_11,
  output out_12,
  output out_13,
  output out_14,
  output out_15,
  output [1:0] out_16,
  output out_17,
  output [5:0] out_18,
  output [7:0] out_19
);

  Multiplexer #(.enable("false")) multiplexer_1 (.in0(in_1), .in1(1'b0), .out(out_11), .sel(in_10));
  Multiplexer #(.enable("false")) multiplexer_2 (.in0(in_2), .in1(1'b0), .out(out_12), .sel(in_10));
  Multiplexer #(.enable("false")) multiplexer_3 (.in0(in_3), .in1(1'b0), .out(out_13), .sel(in_10));
  Multiplexer #(.enable("false")) multiplexer_4 (.in0(in_4), .in1(1'b0), .out(out_14), .sel(in_10));
  Multiplexer #(.enable("false")) multiplexer_5 (.in0(in_5), .in1(1'b0), .out(out_15), .sel(in_10));
  Multiplexer #(.width(2), .enable("false")) multiplexer_6 (.in0(in_6), .in1(2'b00), .out(out_16), .sel(in_10));
  Multiplexer #(.enable("false")) multiplexer_7 (.in0(in_7), .in1(1'b0), .out(out_17), .sel(in_10));
  Multiplexer #(.width(6), .enable("false")) multiplexer_8 (.in0(in_8), .in1({6{1'b0}}), .out(out_18), .sel(in_10));
  Multiplexer #(.width(8), .enable("false")) multiplexer_9 (.in0(in_9), .in1({8{1'b0}}), .out(out_19), .sel(in_10));
endmodule

module EarlyJumpDetection (
  input  [15:0] PC,
  input  [10:0] Imm11,
  input  [15:0] Rs,
  input  [5:0] j_b_control,
  output [15:0] nextPC,
  output nextPCsrc
);

  wire [1:0] or_2_out;
  wire [15:0] adder_1_out, bit_extender_1_out;

  assign bit_extender_1_out = {{5{Imm11[10]}}, Imm11};  // Bit_Extender bit_extender_1
  or or_1 (or_2_out[1], j_b_control[3], j_b_control[5]);
  Adder #(.width(16)) adder_1 (.a(PC), .b(bit_extender_1_out), .out(adder_1_out));  // open: cin, cout
  or or_2 (or_2_out[0], j_b_control[2], j_b_control[4]);
  Multiplexer #(.select(2), .width(16), .enable("false")) multiplexer_1 (
    .in1(adder_1_out), .in2(Rs), .out(nextPC), .sel(or_2_out));  // open: in0, in3
  or or_3 (nextPCsrc, j_b_control[2], j_b_control[3], j_b_control[4], j_b_control[5]);

  // Notes on the sheet:
  //   jalr
  //   j
  //   jr
  //   jal
  //   j&b control: jr, jalr, j, jal, bez, bnz
endmodule
