// Logisim project RegFile.circ as structural Verilog: 1 circuit, main circuit main
module main (
  input  [2:0] RA,
  input  [2:0] RB,
  input  [2:0] RW,
  input  RegWrite,
  input  in_5,
  input  in_6,
  input  [15:0] BusW,
  output [15:0] BusA,
  output [15:0] BusB
);

  wire and_1_out, and_2_out, and_3_out, and_4_out, and_5_out, and_6_out, and_7_out, decoder_1_out1,
       decoder_1_out2, decoder_1_out3, decoder_1_out4, decoder_1_out5, decoder_1_out6, decoder_1_out7,
       decoder_2_out0, decoder_2_out1, decoder_2_out2, decoder_2_out3, decoder_2_out4, decoder_2_out5,
       decoder_2_out6, decoder_2_out7, decoder_3_out0, decoder_3_out1, decoder_3_out2, decoder_3_out3,
       decoder_3_out4, decoder_3_out5, decoder_3_out6, decoder_3_out7;
  wire [15:0] Reg_1_q, Reg_2_q, Reg_3_q, Reg_4_q, Reg_5_q, Reg_6_q, Reg_7_q;

  Decoder #(.select(3), .enable("false")) decoder_1 (
    .out1(decoder_1_out1), .out2(decoder_1_out2), .out3(decoder_1_out3), .out4(decoder_1_out4),
    .out5(decoder_1_out5), .out6(decoder_1_out6), .out7(decoder_1_out7), .sel(RW));  // open: out0
  and and_1 (and_1_out, decoder_1_out1, RegWrite);
  and and_2 (and_2_out, decoder_1_out2, RegWrite);
  and and_3 (and_3_out, decoder_1_out3, RegWrite);
  and and_4 (and_4_out, decoder_1_out4, RegWrite);
  and and_5 (and_5_out, decoder_1_out5, RegWrite);
  and and_6 (and_6_out, decoder_1_out6, RegWrite);
  and and_7 (and_7_out, decoder_1_out7, RegWrite);
  Decoder #(.select(3), .enable("false")) decoder_2 (
    .out0(decoder_2_out0), .out1(decoder_2_out1), .out2(decoder_2_out2), .out3(decoder_2_out3),
    .out4(decoder_2_out4), .out5(decoder_2_out5), .out6(decoder_2_out6), .out7(decoder_2_out7), .sel(RA));
  Register #(.width(16)) Reg_1 (.D(BusW), .en(and_1_out), .Q(Reg_1_q), .clk(in_5), .clr(in_6));
  Register #(.width(16)) Reg_2 (.D(BusW), .en(and_2_out), .Q(Reg_2_q), .clk(in_5), .clr(in_6));
  Register #(.width(16)) Reg_3 (.D(BusW), .en(and_3_out), .Q(Reg_3_q), .clk(in_5), .clr(in_6));
  Register #(.width(16)) Reg_4 (.D(BusW), .en(and_4_out), .Q(Reg_4_q), .clk(in_5), .clr(in_6));
  Register #(.width(16)) Reg_5 (.D(BusW), .en(and_5_out), .Q(Reg_5_q), .clk(in_5), .clr(in_6));
  Register #(.width(16)) Reg_6 (.D(BusW), .en(and_6_out), .Q(Reg_6_q), .clk(in_5), .clr(in_6));
  Register #(.width(16)) Reg_7 (.D(BusW), .en(and_7_out), .Q(Reg_7_q), .clk(in_5), .clr(in_6));
  assign BusA = decoder_2_out0 ? {16{1'b0}} : 16'bz;  // Controlled_Buffer controlled_buffer_1
  assign BusA = decoder_2_out1 ? Reg_1_q : 16'bz;  // Controlled_Buffer controlled_buffer_2
  assign BusA = decoder_2_out2 ? Reg_2_q : 16'bz;  // Controlled_Buffer controlled_buffer_3
  assign BusA = decoder_2_out3 ? Reg_3_q : 16'bz;  // Controlled_Buffer controlled_buffer_4
  assign BusA = decoder_2_out4 ? Reg_4_q : 16'bz;  // Controlled_Buffer controlled_buffer_5
  assign BusA = decoder_2_out5 ? Reg_5_q : 16'bz;  // Controlled_Buffer controlled_buffer_6
  assign BusA = decoder_2_out6 ? Reg_6_q : 16'bz;  // Controlled_Buffer controlled_buffer_7
  assign BusA = decoder_2_out7 ? Reg_7_q : 16'bz;  // Controlled_Buffer controlled_buffer_8
  Decoder #(.select(3), .enable("false")) decoder_3 (
    .out0(decoder_3_out0), .out1(decoder_3_out1), .out2(decoder_3_out2), .out3(decoder_3_out3),
    .out4(decoder_3_out4), .out5(decoder_3_out5), .out6(decoder_3_out6), .out7(decoder_3_out7), .sel(RB));
  assign BusB = decoder_3_out1 ? Reg_1_q : 16'bz;  // Controlled_Buffer controlled_buffer_9
  assign BusB = decoder_3_out2 ? Reg_2_q : 16'bz;  // Controlled_Buffer controlled_buffer_10
  assign BusB = decoder_3_out3 ? Reg_3_q : 16'bz;  // Controlled_Buffer controlled_buffer_11
  assign BusB = decoder_3_out4 ? Reg_4_q : 16'bz;  // Controlled_Buffer controlled_buffer_12
  assign BusB = decoder_3_out5 ? Reg_5_q : 16'bz;  // Controlled_Buffer controlled_buffer_13
  assign BusB = decoder_3_out6 ? Reg_6_q : 16'bz;  // Controlled_Buffer controlled_buffer_14
  assign BusB = decoder_3_out7 ? Reg_7_q : 16'bz;  // Controlled_Buffer controlled_buffer_15
  assign BusB = decoder_3_out0 ? {16{1'b0}} : 16'bz;  // Controlled_Buffer controlled_buffer_16
endmodule
