// Logisim project ShiftBlock.circ as structural Verilog: 1 circuit, main circuit main
module main (
  input  [15:0] Register,
  input  [1:0] ShiftOperation,
  input  [3:0] ShiftAmount,
  output [15:0] Output
);

  wire [15:0] shifter_1_out, shifter_2_out, shifter_3_out, shifter_4_out;

  Shifter #(.width(16)) shifter_1 (.in(Register), .\dist (ShiftAmount), .out(shifter_1_out));
  Shifter #(.width(16), .shift("lr")) shifter_2 (.in(Register), .\dist (ShiftAmount), .out(shifter_2_out));
  Shifter #(.width(16), .shift("ar")) shifter_3 (.in(Register), .\dist (ShiftAmount), .out(shifter_3_out));
  Shifter #(.width(16), .shift("rr")) shifter_4 (.in(Register), .\dist (ShiftAmount), .out(shifter_4_out));
  Multiplexer #(.select(2), .width(16)) multiplexer_1 (
    .in0(shifter_1_out), .in1(shifter_2_out), .in2(shifter_3_out), .in3(shifter_4_out), .out(Output),
    .sel(ShiftOperation), .en(1'b1));
endmodule
