// Logisim project SingleCycle.circ as structural Verilog: 1 circuit, main circuit main
module main (
  input  in_1,
  input  in_2,
  input  in_3,
  input  reset
);

  wire ALUSrc, clock_1_out, jal, main_5_flag, MemRead, MemRed, MemWrite, PcSrc, RegDst, RegWrite, setOp,
       SignExt;
  wire [1:0] func, MemToReg;
  wire [2:0] main_2_rd, main_2_rs, main_2_rt, multiplexer_2_out, multiplexer_3_out;
  wire [4:0] main_2_imm_5, OP;
  wire [5:0] NextPcControl;
  wire [7:0] ALUOp, Imm8;
  wire [10:0] main_2_imm_11;
  wire [15:0] BusB, jalr, main_3_output, main_4_busa, main_5_result, main_7_out_4, multiplexer_1_out,
       multiplexer_4_out, multiplexer_5_out, nextPC, ram_1_data, register_1_q, rom_1_data;

  Multiplexer #(.width(16), .enable("false")) multiplexer_1 (
    .in0(jalr), .in1(nextPC), .out(multiplexer_1_out), .sel(PcSrc));
  Register #(.width(16)) register_1 (
    .D(multiplexer_1_out), .en(in_1), .Q(register_1_q), .clk(clock_1_out), .clr(reset));
  ControlUnit_main main_1 (
    .opCode(OP), .func(func), .RegDst(RegDst), .RegWrite(RegWrite), .signExt(SignExt), .ALUsrc(ALUSrc),
    .MemRead(MemRead), .MemWrite(MemWrite), .setOp(setOp), .MemToReg(MemToReg), .ALUOp(ALUOp),
    .NextPcControl(NextPcControl), .jal(jal));
  Adder #(.width(16)) adder_1 (.a(16'h1), .b(register_1_q), .out(jalr));  // open: cin, cout
  ROM #(.addrWidth(16), .dataWidth(16)) rom_1 (.addr(register_1_q), .data(rom_1_data), .sel(in_2));
  Splitter_main main_2 (
    .Rt(main_2_rt), .Rs(main_2_rs), .Rd(main_2_rd), .f(func), .Op(OP), .Imm_5(main_2_imm_5), .Imm_8(Imm8),
    .Imm_11(main_2_imm_11), .in_1(rom_1_data));
  // Probe on main_2_rd
  // Probe on main_2_rt
  // Probe on main_2_rd
  Multiplexer #(.width(3), .enable("false")) multiplexer_2 (
    .in0(main_2_rt), .in1(main_2_rd), .out(multiplexer_2_out), .sel(RegDst));
  Clock clock_1 (.out(clock_1_out));
  Ext_main main_3 (.Imm_5(main_2_imm_5), .Output(main_3_output), .ExtSrc(SignExt));
  Multiplexer #(.width(3), .enable("false")) multiplexer_3 (
    .in0(multiplexer_2_out), .in1(3'b111), .out(multiplexer_3_out), .sel(jal));
  // Probe on main_4_busa
  RegFile_main main_4 (
    .RA(main_2_rs), .RB(main_2_rt), .RW(multiplexer_3_out), .BusW(multiplexer_5_out), .RegWrite(RegWrite),
    .BusA(main_4_busa), .BusB(BusB), .in_5(clock_1_out), .in_6(reset));
  // Probe on multiplexer_5_out
  // Probe on BusB
  ALU_main main_5 (
    .inputA(main_4_busa), .inputB(multiplexer_4_out), .ALUControl(ALUOp), .result(main_5_result),
    .Flag(main_5_flag));
  Multiplexer #(.width(16), .enable("false")) multiplexer_4 (
    .in0(BusB), .in1(main_3_output), .out(multiplexer_4_out), .sel(ALUSrc));
  Multiplexer #(.select(2), .width(16), .enable("false")) multiplexer_5 (
    .in0(main_5_result), .in1(ram_1_data), .in2(main_7_out_4), .in3(jalr), .out(multiplexer_5_out),
    .sel(MemToReg));
  // nextPC_main main_6: pin names not known; wires that end beside it: register_1_q, main_2_imm_11, main_4_busa, nextPC, main_5_flag, PcSrc, NextPcControl
  RAM #(.addrWidth(16), .dataWidth(16), .bus("separate")) ram_1 (
    .addr(main_5_result), .din(BusB), .data(ram_1_data), .str(MemWrite), .sel(1'b1), .clk(clock_1_out),
    .ld(MemRed), .clr(in_3));
  set_main main_7 (.Imm_8(Imm8), .BusB(BusB), .out_4(main_7_out_4), ._0__set___1__SetH(setOp));

  // Notes on the sheet:
  //   PcSrc
  //   contents of rom_1 (hex, n*v repeats v):
  //   2049 8811 6293 2049 2052 cfe3 edb e92 8013 123 2052 6294 cfe4
endmodule
