// Logisim project Splitter.circ as structural Verilog: 1 circuit, main circuit main
module main (
  input  [15:0] in_1,
  output [2:0] Rt,
  output [2:0] Rs,
  output [2:0] Rd,
  output [1:0] f,
  output [4:0] Op,
  output [4:0] Imm_5,
  output [7:0] Imm_8,
  output [10:0] Imm_11
);


  assign f = in_1[10:9];
  assign Imm_5 = in_1[10:6];
  assign Imm_8 = in_1[10:3];
  assign Imm_11 = in_1[10:0];
  assign Op = in_1[15:11];
  assign Rd = in_1[8:6];
  assign Rs = in_1[5:3];
  assign Rt = in_1[2:0];

  // Notes on the sheet:
  //   R-type
  //   I-type
  //   B-type
  //   J-type
endmodule
