// Logisim project nextPC.circ as structural Verilog: 1 circuit, main circuit main
module main (
  input  [15:0] PC,
  input  [10:0] Imm11,
  input  flag,
  input  [5:0] j_b_control,
  output [15:0] nextPC,
  output nextPCsrc
);

  wire and_1_out, and_2_out;
  wire [15:0] bit_extender_1_out;

  assign bit_extender_1_out = {{8{Imm11[10]}}, Imm11[10:3]};  // Bit_Extender bit_extender_1
  and and_1 (and_1_out, ~flag, j_b_control[0]);  // AND_Gate
  and and_2 (and_2_out, flag, j_b_control[1]);
  Adder #(.width(16)) adder_1 (.a(PC), .b(bit_extender_1_out), .out(nextPC));  // open: cin, cout
  or or_1 (nextPCsrc, and_1_out, and_2_out);

  // Notes on the sheet:
  //   bnz
  //   Branch Imm8
  //   bez
  //   j&b control: jr, jalr, j, jal, bez, bnz
endmodule
