// Logisim project set.circ as structural Verilog: 1 circuit, main circuit main
module main (
  input  [7:0] Imm_8,
  input  _0__set___1__SetH,
  input  [15:0] BusB,
  output [15:0] out_4
);

  wire [15:0] bit_extender_1_out;

  assign bit_extender_1_out = {{8{Imm_8[7]}}, Imm_8};  // Bit_Extender bit_extender_1
  Multiplexer #(.width(16), .enable("false")) multiplexer_1 (
    .in0(bit_extender_1_out), .in1({Imm_8, BusB[7:0]}), .out(out_4), .sel(_0__set___1__SetH));
endmodule
